# Fritzing sketch circuitDiagram (saved by Fritzing 0.8.5b)
breadboards: 1

parts:
  Uno_R3/_Ruggeduino = Arduino Uno (Rev3)
  R1 = Resistor [tolerance=±5% resistance=10k package=THT]
  J1 = Basic Servo
  yStepper = Stepper Motor - Unipolar [part_number=1-19-4202]
  xStepper = Stepper Motor - Bipolar [part_number="\t17HS13-0404S"]
  S3 = SWITCH-MOMENTARY-2 [package=tactile-switch-1101ne]
  R2 = Resistor [tolerance=±5% resistance=10k package=THT]
  S4 = SWITCH-MOMENTARY-2 [package=tactile-switch-1101ne]
  Adafruit_Motor_Shield = Rotoshield - Motor driver shield for Arduino

nets:
  N1: Uno_R3/_Ruggeduino.A4/SDA, Adafruit_Motor_Shield.A_IN_4
  N2: Uno_R3/_Ruggeduino.A5/SCL, Adafruit_Motor_Shield.A_IN_5
  GND: Uno_R3/_Ruggeduino.GND, R1.Pin_1, J1.gnd, yStepper.COMMON_1, yStepper.COMMON_2, R2.Pin_1, Adafruit_Motor_Shield.GND
  N3: R1.Pin_0, S3.2, Adafruit_Motor_Shield.DIG_8
  VCC: J1.vcc, S3.1, S4.1, Adafruit_Motor_Shield.+5V
  N4: J1.pulse, Adafruit_Motor_Shield.DIG_9
  N5: yStepper.A, Adafruit_Motor_Shield.M4-1
  N6: yStepper.C, Adafruit_Motor_Shield.M4-2
  N7: yStepper.B, Adafruit_Motor_Shield.M3-1
  N8: yStepper.D, Adafruit_Motor_Shield.M3-2
  N9: xStepper.A, Adafruit_Motor_Shield.M1-1
  N10: xStepper.C, Adafruit_Motor_Shield.M1-2
  N11: xStepper.B, Adafruit_Motor_Shield.M2-1
  N12: xStepper.D, Adafruit_Motor_Shield.M2-2
  N13: R2.Pin_0, S4.2, Adafruit_Motor_Shield.DIG_2
  12V: Adafruit_Motor_Shield.VCC
